# Fritzing sketch Sketch (saved by Fritzing 0.9.2b)
circuit board: 6.9125cm x 5.57257cm
breadboards: 1

parts:
  Part1 = Arduino Uno (Rev3)
  RHT1 = Humidity and Temperature Sensor RHT03
  R1 = Resistor [tolerance=±5% resistance=10k package=THT]
  7_Segment_4_Digit_Display1 = 7-SEGMENT-4DIGIT common anode [part_number="5461BS - 5462BS" package=7-segment-4digit-anode]
  U1 = 74HC595 [package="DIP16 [THT]"]

nets:
  N1: Part1.D9_PWM, 7_Segment_4_Digit_Display1.D1
  N2: Part1.D10_PWM/SS, 7_Segment_4_Digit_Display1.D2
  N3: Part1.D11_PWM/MOSI, 7_Segment_4_Digit_Display1.D3
  N4: Part1.D12/MISO, 7_Segment_4_Digit_Display1.D4
  GND: Part1.GND, RHT1.GND_2, U1.GND, U1.OE
  N5: Part1.D2, RHT1.Data-signal, R1.Pin_0
  N6: Part1.D3_PWM, U1.DS
  N7: Part1.D4, U1.ST_CP
  N8: Part1.D5_PWM, U1.SH_CP
  VCC: Part1.5V, RHT1.Vcc, R1.Pin_1, U1.MR, U1.VCC
  N9: 7_Segment_4_Digit_Display1.E, U1.Q5
  N10: 7_Segment_4_Digit_Display1.D, U1.Q4
  N11: 7_Segment_4_Digit_Display1.DP, U1.Q0
  N12: 7_Segment_4_Digit_Display1.C, U1.Q3
  N13: 7_Segment_4_Digit_Display1.G, U1.Q7
  N14: 7_Segment_4_Digit_Display1.B, U1.Q2
  N15: 7_Segment_4_Digit_Display1.F, U1.Q6
  N16: 7_Segment_4_Digit_Display1.A, U1.Q1

custom parts:
  7-SEGMENT-4DIGIT common anode: A 7 Segment 4 Digit common anode display, with decimal points
